// Logisim project somador.circ as structural Verilog
module main (
  input  A0,
  input  A1,
  input  A2,
  input  Ci__Sempre_Zero,
  input  A3,
  input  B0,
  input  B1,
  input  B2,
  input  B3,
  output S0,
  output S1,
  output S2,
  output S3
);

  wire Decodificador_2_a, Decodificador_2_b, Decodificador_2_c, Decodificador_2_d, Decodificador_2_e,
       Decodificador_2_f, Decodificador_2_g, Decodificador_3_a, Decodificador_3_b, Decodificador_3_c,
       Decodificador_3_d, Decodificador_3_e, Decodificador_3_f, Decodificador_3_g, Decodificador_a,
       Decodificador_b, Decodificador_c, Decodificador_d, Decodificador_e, Decodificador_f, Decodificador_g;

  Somador_4_bits Somador_4_bits (
    .Sempre_Zero(Ci__Sempre_Zero), .A0(A0), .B0(B0), .A1(A1), .B1(B1), .A2(A2), .B2(B2), .in_8(A3), .B3(B3),
    .S0(S0), .S1(S1), .S2(S2), .S3(S3));
  Decodiicador Decodificador (
    .E0(A0), .E1(A1), .E2(A2), .E3(A3), .a(Decodificador_a), .b(Decodificador_b), .c(Decodificador_c),
    .d(Decodificador_d), .e(Decodificador_e), .f(Decodificador_f), .g(Decodificador_g));
  Decodiicador Decodificador_2 (
    .E0(B0), .E1(B1), .E2(B2), .E3(B3), .a(Decodificador_2_a), .b(Decodificador_2_b), .c(Decodificador_2_c),
    .d(Decodificador_2_d), .e(Decodificador_2_e), .f(Decodificador_2_f), .g(Decodificador_2_g));
  Decodiicador Decodificador_3 (
    .E0(S0), .E1(S1), .E2(S2), .E3(S3), .a(Decodificador_3_a), .b(Decodificador_3_b), .c(Decodificador_3_c),
    .d(Decodificador_3_d), .e(Decodificador_3_e), .f(Decodificador_3_f), .g(Decodificador_3_g));
  _7_Segment_Display u_7_segment_display_1 (
    .g(Decodificador_g), .f(Decodificador_f), .a(Decodificador_a), .b(Decodificador_b), .e(Decodificador_e),
    .d(Decodificador_d), .c(Decodificador_c));  // open: dp
  _7_Segment_Display u_7_segment_display_2 (
    .g(Decodificador_2_g), .f(Decodificador_2_f), .a(Decodificador_2_a), .b(Decodificador_2_b),
    .e(Decodificador_2_e), .d(Decodificador_2_d), .c(Decodificador_2_c));  // open: dp
  _7_Segment_Display u_7_segment_display_3 (
    .g(Decodificador_3_g), .f(Decodificador_3_f), .a(Decodificador_3_a), .b(Decodificador_3_b),
    .e(Decodificador_3_e), .d(Decodificador_3_d), .c(Decodificador_3_c));  // open: dp
endmodule

module Decodiicador (
  input  E0,
  input  E1,
  input  E2,
  input  E3,
  output a,
  output b,
  output c,
  output d,
  output e,
  output f,
  output g
);

  wire and_1_out, and_2_out, and_3_out, and_4_out, and_5_out, and_6_out, and_7_out, and_8_out, and_9_out,
       and_10_out, and_11_out, and_12_out, and_13_out, and_14_out, and_15_out, and_16_out, and_17_out,
       and_18_out, and_19_out, and_20_out, and_21_out, and_22_out, and_23_out, and_24_out, and_25_out,
       and_26_out, and_27_out, and_28_out, and_29_out, and_30_out, and_31_out, and_32_out, and_33_out,
       and_34_out, and_35_out, and_36_out, and_37_out, and_38_out, and_39_out, and_40_out, and_41_out,
       and_42_out, and_43_out, and_44_out, not_1_out, not_2_out, not_3_out, not_4_out, not_5_out, not_6_out,
       not_7_out, not_8_out, not_9_out, not_10_out, not_11_out, not_12_out, not_13_out, not_14_out,
       not_15_out, not_16_out, not_17_out, not_18_out, not_19_out, not_20_out, not_21_out, not_22_out,
       not_23_out, not_24_out, not_25_out, not_26_out, not_27_out, not_28_out, not_29_out, not_30_out,
       not_31_out, not_32_out, not_33_out, not_34_out, not_35_out, not_36_out, not_37_out, not_38_out,
       not_39_out, not_40_out, not_41_out, not_42_out, or_1_out, or_2_out, or_3_out, or_4_out, or_5_out,
       or_6_out, or_7_out, or_8_out, or_9_out, or_10_out, or_11_out, or_12_out, or_14_out, or_17_out,
       or_18_out, or_20_out, or_21_out, or_22_out, or_23_out;

  not not_1 (not_1_out, E1);
  and and_1 (and_1_out, not_1_out, not_2_out);
  not not_2 (not_2_out, E3);
  not not_3 (not_3_out, E0);
  and and_2 (and_2_out, not_3_out, E2);
  not not_4 (not_4_out, E0);
  and and_3 (and_3_out, not_4_out, E1);
  and and_4 (and_4_out, E0, not_5_out);
  not not_5 (not_5_out, E1);
  not not_6 (not_6_out, E2);
  not not_7 (not_7_out, E0);
  not not_8 (not_8_out, E1);
  not not_9 (not_9_out, E0);
  and and_5 (and_5_out, not_9_out, not_10_out);
  not not_10 (not_10_out, E2);
  not not_11 (not_11_out, E3);
  not not_12 (not_12_out, E0);
  not not_13 (not_13_out, E2);
  not not_14 (not_14_out, E0);
  and and_6 (and_6_out, not_14_out, not_15_out);
  not not_15 (not_15_out, E2);
  not not_16 (not_16_out, E0);
  and and_7 (and_7_out, not_16_out, E3);
  not not_17 (not_17_out, E2);
  not not_18 (not_18_out, E0);
  not not_19 (not_19_out, E1);
  not not_20 (not_20_out, E0);
  and and_8 (and_8_out, not_20_out, not_21_out);
  not not_21 (not_21_out, E1);
  not not_22 (not_22_out, E3);
  not not_23 (not_23_out, E1);
  and and_9 (and_9_out, not_23_out, E2);
  not not_24 (not_24_out, E2);
  not not_25 (not_25_out, E1);
  and and_10 (and_10_out, not_25_out, not_26_out);
  not not_26 (not_26_out, E3);
  and and_11 (and_11_out, E2, not_27_out);
  not not_27 (not_27_out, E3);
  and and_12 (and_12_out, E0, E2);
  and and_13 (and_13_out, E0, E1);
  not not_28 (not_28_out, E0);
  and and_14 (and_14_out, not_28_out, not_29_out);
  not not_29 (not_29_out, E2);
  not not_30 (not_30_out, E3);
  not not_31 (not_31_out, E0);
  and and_15 (and_15_out, not_31_out, E1);
  not not_32 (not_32_out, E2);
  not not_33 (not_33_out, E0);
  not not_34 (not_34_out, E1);
  and and_16 (and_16_out, not_34_out, E2);
  and and_17 (and_17_out, E1, not_35_out);
  not not_35 (not_35_out, E2);
  and and_18 (and_18_out, E1, not_36_out);
  not not_36 (not_36_out, E3);
  or or_1 (or_1_out, and_1_out, and_2_out);
  and and_19 (and_19_out, and_3_out, E3);
  and and_20 (and_20_out, E1, E2);
  and and_21 (and_21_out, and_4_out, not_6_out);
  and and_22 (and_22_out, not_7_out, not_8_out);
  and and_23 (and_23_out, and_5_out, not_11_out);
  not not_37 (not_37_out, E1);
  not not_38 (not_38_out, E3);
  and and_24 (and_24_out, not_12_out, E2);
  and and_25 (and_25_out, E0, not_13_out);
  or or_2 (or_2_out, and_6_out, and_7_out);
  and and_26 (and_26_out, not_17_out, E3);
  and and_27 (and_27_out, not_18_out, E1);
  and and_28 (and_28_out, E0, not_19_out);
  and and_29 (and_29_out, and_8_out, not_22_out);
  and and_30 (and_30_out, and_9_out, E3);
  and and_31 (and_31_out, E1, not_24_out);
  and and_32 (and_32_out, E1, E2);
  not not_39 (not_39_out, E3);
  not not_40 (not_40_out, E2);
  or or_3 (or_3_out, and_10_out, and_11_out);
  or or_4 (or_4_out, and_12_out, and_13_out);
  and and_33 (and_33_out, and_14_out, not_30_out);
  and and_34 (and_34_out, and_15_out, not_32_out);
  and and_35 (and_35_out, not_33_out, E1);
  not not_41 (not_41_out, E3);
  not not_42 (not_42_out, E1);
  or or_5 (or_5_out, and_16_out, and_17_out);
  or or_6 (or_6_out, and_18_out, E0);
  or or_7 (or_7_out, or_1_out, and_19_out);
  or or_8 (or_8_out, and_20_out, and_21_out);
  or or_9 (or_9_out, and_22_out, and_23_out);
  and and_36 (and_36_out, not_37_out, not_38_out);
  and and_37 (and_37_out, and_24_out, E3);
  and and_38 (and_38_out, and_25_out, E3);
  or or_10 (or_10_out, or_2_out, and_26_out);
  or or_11 (or_11_out, and_27_out, and_28_out);
  or or_12 (or_12_out, and_29_out, and_30_out);
  and and_39 (and_39_out, and_31_out, E3);
  and and_40 (and_40_out, and_32_out, not_39_out);
  and and_41 (and_41_out, E0, not_40_out);
  or or_13 (e, or_3_out, or_4_out);
  or or_14 (or_14_out, and_33_out, and_34_out);
  and and_42 (and_42_out, and_35_out, not_41_out);
  and and_43 (and_43_out, E0, not_42_out);
  and and_44 (and_44_out, E0, E2);
  or or_15 (g, or_5_out, or_6_out);
  or or_16 (a, or_7_out, or_8_out);
  or or_17 (or_17_out, or_9_out, and_36_out);
  or or_18 (or_18_out, and_37_out, and_38_out);
  or or_19 (c, or_10_out, or_11_out);
  or or_20 (or_20_out, or_12_out, and_39_out);
  or or_21 (or_21_out, and_40_out, and_41_out);
  or or_22 (or_22_out, or_14_out, and_42_out);
  or or_23 (or_23_out, and_43_out, and_44_out);
  or or_24 (b, or_17_out, or_18_out);
  or or_25 (d, or_20_out, or_21_out);
  or or_26 (f, or_22_out, or_23_out);
endmodule

module Somador_1_2 (
  input  a,
  input  b,
  output soma,
  output vai1
);

  xor xor_1 (soma, a, b);
  and and_1 (vai1, a, b);
endmodule

module Somador_Completo (
  input  Ci,
  input  a,
  input  b,
  output S,
  output c01
);

  wire somador_1_2_1_soma, somador_1_2_1_vai1, somador_1_2_2_vai1;

  Somador_1_2 somador_1_2_1 (.a(a), .b(b), .soma(somador_1_2_1_soma), .vai1(somador_1_2_1_vai1));
  Somador_1_2 somador_1_2_2 (.a(Ci), .b(somador_1_2_1_soma), .soma(S), .vai1(somador_1_2_2_vai1));
  or or_1 (c01, somador_1_2_2_vai1, somador_1_2_1_vai1);
endmodule

module Somador_4_bits (
  input  Sempre_Zero,
  input  A0,
  input  B0,
  input  A1,
  input  B1,
  input  A2,
  input  B2,
  input  in_8,
  input  B3,
  output S0,
  output S1,
  output S2,
  output S3
);

  wire somador_completo_1_c01, somador_completo_2_c01, somador_completo_3_c01;

  Somador_Completo somador_completo_1 (.Ci(Sempre_Zero), .a(A0), .b(B0), .S(S0), .c01(somador_completo_1_c01));
  Somador_Completo somador_completo_2 (
    .Ci(somador_completo_1_c01), .a(A1), .b(B1), .S(S1), .c01(somador_completo_2_c01));
  Somador_Completo somador_completo_3 (
    .Ci(somador_completo_2_c01), .a(A2), .b(B2), .S(S2), .c01(somador_completo_3_c01));
  Somador_Completo somador_completo_4 (.Ci(somador_completo_3_c01), .a(in_8), .b(B3), .S(S3));  // open: c01
endmodule
